# Fritzing sketch NFC Audio Box (saved by Fritzing 0.9.3b)
breadboards: 1

parts:
  Composant1 = Arduino Nano (Rev3.0)
  Composant2 = RFID-RC522-v2
  DFRobot_DFPlayer_Mini1 = DFRobot DFPlayer Mini [part_number=DFR0299]
  VCC1 = Battery block 9V
  Grove1 = Grove OLED 128x96
  S1 = Pushbutton [package="[THT]"]
  S2 = Pushbutton [package="[SMD]"]
  S3 = Pushbutton [package="[SMD]"]
  S4 = Pushbutton [package="[SMD]"]
  S5 = Pushbutton [package="[SMD]"]
  S6 = Round Pushbutton
  R1 = Resistor [tolerance=±5% resistance=1k package="2010 [SMD]"]
  J1 = Piezo Speaker

nets:
  GND: Composant1.GND, Composant2.GND, DFRobot_DFPlayer_Mini1.GND-1, DFRobot_DFPlayer_Mini1.GND-2, VCC1.-, Grove1.GND
  N1: Composant1.D2, S4.Pin_3, S4.Pin_4
  N2: Composant1.D3, S3.Pin_3, S3.Pin_4, S4.Pin_1, S4.Pin_2, S5.Pin_1, S5.Pin_2
  N3: Composant1.D4, S5.Pin_3, S5.Pin_4
  N4: Composant1.D6, DFRobot_DFPlayer_Mini1.TX
  N5: Composant1.D7, R1.Pin_1
  N6: Composant1.D8, S2.Pin_3, S2.Pin_4
  N7: Composant1.D9, S1.Pin_3, S1.Pin_4
  N8: Composant1.D10, Composant2.SDA
  N9: Composant1.D11/MOSI, Composant2.MOSI
  N10: Composant1.D12/MISO, Composant2.MISO
  N11: Composant1.VIN, S6.leg1
  VCC: Composant1.5V, DFRobot_DFPlayer_Mini1.VCC, Grove1.VCC
  N12: Composant1.A5, Grove1.SDA
  N13: Composant1.A4, Grove1.SCL
  3V3: Composant1.3V3, Composant2.3.3V
  N14: Composant1.D13/SCK, Composant2.SCK
  N15: DFRobot_DFPlayer_Mini1.RX, R1.Pin_0
  N16: DFRobot_DFPlayer_Mini1.SPK_1, J1.pin2
  N17: DFRobot_DFPlayer_Mini1.SPK_2, J1.pin1
  N18: VCC1.+, S6.leg0
  N19: S1.Pin_1, S1.Pin_2, S2.Pin_1, S2.Pin_2, S3.Pin_1, S3.Pin_2

custom parts:
  RFID-RC522-v2: A simple China made RFID-RC522 Reader; do check the pin labels, as this is a MFRC522 based clone.
